# Fritzing sketch camera_flash_connector (saved by Fritzing 0.9.3b)

parts:
  R1 = Resistor [tolerance=±5% resistance=330 package=THT]
  PC817 = Sharp PC817 [package=THT]
  3_5mm_Jack = 3.5mm Audio Jack [package=audio-jack]
  PC817_2 = Sharp PC817 [package=THT]
  3_5mm_Jack_2 = 3.5mm Audio Jack [package=audio-jack]
  R2 = Resistor [tolerance=±5% resistance=330 package=THT]

nets:
  N1: R1.Pin_0, PC817.Pin_1
  GND: PC817.Pin_2, PC817_2.Pin_2
  N2: PC817.Pin_4, 3_5mm_Jack.LEFT
  N3: PC817.Pin_3, 3_5mm_Jack.SLEEVE
  N4: PC817_2.Pin_1, R2.Pin_0
  N5: PC817_2.Pin_4, 3_5mm_Jack_2.LEFT
  N6: PC817_2.Pin_3, 3_5mm_Jack_2.SLEEVE

notes:
  Red pin
  Blue pin
  Brown pin
  Flash Trigger
  Camera Trigger
  Camera and Flash Connector
