# Fritzing sketch coin_dropper (saved by Fritzing 0.9.3b)

parts:
  Part1 = Arduino Uno (Rev3)
  Coin_Gate = Basic Servo
  Start_Button = Pushbutton [package="[THT]"]
  R1 = Resistor [tolerance=±5% resistance=10k package=THT]
  Phototransistor_Gate = LTR-301 [package=ltr-301]
  R2 = Resistor [tolerance=±5% resistance=220 package=THT]
  LED1 = LED - 5mm [color="Red (633nm)" package="5 mm [THT]"]
  R3 = Resistor [tolerance=±5% resistance=220 package=THT]

nets:
  N1: Part1.A0, Phototransistor_Gate.E
  N2: Part1.D9_PWM, Coin_Gate.pulse
  N3: Part1.D2, Start_Button.Pin_2, R1.Pin_0
  5V: Part1.5V, Coin_Gate.vcc, Start_Button.Pin_3, Start_Button.Pin_4, R2.Pin_0, R3.Pin_0
  GND: Coin_Gate.gnd, R1.Pin_1, LED1.cathode
  N4: Phototransistor_Gate.C, R2.Pin_1
  N5: LED1.anode, R3.Pin_1

notes:
  Coin Dropper
